// Logisim project 12.circ as structural Verilog: 1 circuit, main circuit main
module main (
  input  WRITE,
  input  READ,
  input  in_3,
  input  [2:0] S,
  input  in_5,
  input  in_6,
  input  in_7,
  input  in_8,
  input  [3:0] CONTROL,
  input  in_10
);

  wire ALU_e, clock_1_out;
  wire [11:0] AR_q, PC_q;
  wire [15:0] AC_q, ALU_out_4, bit_extender_1_out, bit_extender_2_out, DR_q, IR_q, multiplexer_1_out,
       ram_1_data, TR_q;

  D_Flip_Flop E (.clk(clock_1_out), .D(ALU_e));  // open: Q, Qn, preset, en, reset
  Clock clock_1 (.out(clock_1_out));
  Counter #(.width(12), .max('hfff)) AR (
    .load(in_3), .D(multiplexer_1_out[11:0]), .Q(AR_q), .clk(clock_1_out));  // open: count, carry, clr
  Counter #(.width(12), .max('hfff)) PC (
    .load(in_5), .D(multiplexer_1_out[11:0]), .Q(PC_q), .clk(clock_1_out));  // open: count, carry, clr
  Counter #(.width(16), .max('hffff)) DR (
    .load(in_6), .D(multiplexer_1_out), .Q(DR_q), .clk(clock_1_out));  // open: count, carry, clr
  T17_31_1543_S2_main ALU (.in_1(DR_q), .in_2(AC_q), .E(ALU_e), .S(CONTROL), .out_4(ALU_out_4));
  Counter #(.width(16), .max('hffff)) IR (
    .load(in_8), .D(multiplexer_1_out), .Q(IR_q), .clk(clock_1_out));  // open: count, carry, clr
  Counter #(.width(16), .max('hffff)) TR (
    .load(in_10), .D(multiplexer_1_out), .Q(TR_q), .clk(clock_1_out));  // open: count, carry, clr
  RAM #(.addrWidth(12), .dataWidth(16), .bus("separate")) ram_1 (
    .addr(AR_q), .din(multiplexer_1_out), .data(ram_1_data), .str(WRITE), .clk(clock_1_out), .ld(READ));  // open: sel, clr
  assign bit_extender_1_out = {{4{1'b0}}, AR_q};  // Bit_Extender bit_extender_1
  assign bit_extender_2_out = {{4{1'b0}}, PC_q};  // Bit_Extender bit_extender_2
  Counter #(.width(16), .max('hffff)) AC (.load(in_7), .D(ALU_out_4), .Q(AC_q));  // open: count, carry, clk, clr
  Multiplexer #(.select(3), .width(16), .enable("false")) multiplexer_1 (
    .in1(bit_extender_1_out), .in2(bit_extender_2_out), .in3(DR_q), .in4(AC_q), .in5(IR_q), .in6(TR_q),
    .in7(ram_1_data), .out(multiplexer_1_out), .sel(S));  // open: in0
endmodule
