// Logisim project ALU encoder_17609.circ as structural Verilog: 1 circuit, main circuit main
module main (
  input  AND,
  input  ADD,
  input  Transfer_DR,
  input  COM,
  input  CIL,
  input  CIR,
  output [3:0] out_7
);

  Priority_Encoder #(.select(4)) priority_encoder_1 (
    .in0(AND), .in1(1'b0), .in2(1'b0), .in3(COM), .in4(1'b0), .in5(1'b0), .in6(CIL), .in7(CIR), .in8(1'b0),
    .in9(1'b0), .in10(ADD), .in11(1'b0), .in12(1'b0), .in13(1'b0), .in14(1'b0), .in15(Transfer_DR),
    .out(out_7));

  // Notes on the sheet:
  //   The role of the encoder is to 
  //   convert the control signals to selection lines
  //   that are not present inside the BC ALU
  //   were replaced witha constant signal of 0
  //   since they can never be selected
  //   so, in the process, the arithmetic/ logical/ shift operations
endmodule
