// Logisim project Control.circ as structural Verilog: 1 circuit, main circuit main
module main (
  input  CLK,
  input  [15:0] IR,
  input  [15:0] DR,
  output LDAC,
  output CLAC,
  output [2:0] BUS,
  output WRITE,
  output READ,
  output LDPC,
  output LDAR,
  output LDDR,
  output LDIR,
  output TransferDR,
  output ADD,
  output PCINC
);

  wire and_1_out, and_2_out, and_3_out, and_4_out, and_5_out, and_6_out, and_10_out, and_11_out, and_12_out,
       and_13_out, and_14_out, and_15_out, and_16_out, and_17_out, and_18_out, and_19_out, D0, D1, D2, D3,
       D4, D5, D6, D7, I, not_1_out, not_2_out, not_3_out, not_4_out, not_5_out, not_6_out, or_1_out,
       or_2_out, or_3_out, or_4_out, T0, T2, T3, T4, T5, T6, T7, T8, T9, T10, T11, T12, T13, T14, T15, X1,
       X3, X4;
  wire [3:0] SC_q;

  and and_1 (and_1_out, D4, T4);
  Counter #(.width(4), .max('hf)) SC (.count(1'b1), .Q(SC_q), .clk(CLK), .clr(or_1_out));  // open: load, D, carry
  or or_1 (or_1_out, and_1_out, and_2_out, and_3_out, and_4_out, and_5_out, and_6_out);
  and and_2 (and_2_out, D3, T4);
  and and_3 (and_3_out, D2, T5);
  and and_4 (and_4_out, D1, T5);
  and and_5 (and_5_out, D6, T6);
  D_Flip_Flop u_I (.clk(CLK), .D(IR[15]), .Q(I));  // open: Qn, preset, en, reset
  Decoder #(.select(3), .enable("false")) decoder_1 (
    .out0(D0), .out1(D1), .out2(D2), .out3(D3), .out4(D4), .out5(D5), .out6(D6), .out7(D7), .sel(IR[14:12]));
  Decoder #(.select(4), .enable("false")) decoder_2 (
    .out0(T0), .out1(LDIR), .out2(T2), .out3(T3), .out4(T4), .out5(T5), .out6(T6), .out7(T7), .out8(T8),
    .out9(T9), .out10(T10), .out11(T11), .out12(T12), .out13(T13), .out14(T14), .out15(T15), .sel(SC_q));
  and and_6 (and_6_out, D7, not_1_out, T3, not_2_out);
  not not_1 (not_1_out, I);
  or or_2 (or_2_out, DR[0], DR[1], DR[2], DR[3], DR[4], DR[5], DR[6], DR[7], DR[8], DR[9], DR[10], DR[11], DR[12], DR[13], DR[14], DR[15]);
  not not_2 (not_2_out, or_2_out);
  not not_3 (not_3_out, I);
  and and_7 (LDPC, D4, T4);
  not not_4 (not_4_out, I);
  not not_5 (not_5_out, D7);
  not not_6 (not_6_out, D7);
  and and_8 (TransferDR, T5, D2);
  and and_9 (ADD, T5, D1);
  and and_10 (and_10_out, not_2_out, D7, not_3_out, T3);
  and and_11 (and_11_out, D1, T5);
  and and_12 (and_12_out, T5, D2);
  and and_13 (and_13_out, D3, T4);
  and and_14 (and_14_out, D6, T6);
  and and_15 (and_15_out, not_5_out, I, T3);
  and and_16 (and_16_out, T4, or_3_out);
  or or_3 (or_3_out, D0, D1, D2, D6);
  and and_17 (and_17_out, not_6_out, I, T3);
  and and_18 (and_18_out, T4, or_4_out);
  or or_4 (or_4_out, D1, D6);
  and and_19 (and_19_out, D6, T5);
  or or_5 (PCINC, and_10_out, LDIR);
  or or_6 (LDAC, and_11_out, and_12_out);
  and and_20 (CLAC, D7, not_4_out, T3, IR[11]);
  or or_7 (WRITE, and_13_out, and_14_out);
  or or_8 (READ, LDIR, and_15_out, and_16_out);
  or or_9 (LDAR, and_17_out, T0);
  or or_10 (LDDR, and_18_out, and_19_out);
  and and_21 (X4, D3, T4);
  and and_22 (X1, D4, T4);
  and and_23 (X3, D6, T6);
  Priority_Encoder priority_encoder_1 (
    .in1(X1), .in2(T0), .in3(X3), .in4(X4), .in5(1'b0), .in6(1'b0), .in7(READ), .out(BUS), .en_in(1'b1));  // open: in0, gs, en_out

  // Other names for the same wires on the sheet: T1 = LDIR; X2 = T0
endmodule
