// Logisim project Milestone 1_bitwise _17611.circ as structural Verilog: 3 circuits, main circuit ALU_Combined
// ALU
module ALU_Combined (
  input  E,
  input  AND,
  input  ADD,
  input  DR,
  input  COM,
  input  CIR,
  input  CIL,
  input  [15:0] AC,
  input  [15:0] DR_2,
  output [15:0] AC_2,
  output E_2
);

  wire and_1_out, and_2_out, and_3_out, C0, C1, C2, C3, C4, C5, C6, C7, C8, C9, C10, C11, C12, C13, C14,
       E_ADD;

  and and_1 (and_1_out, AC[15], CIR);
  and and_2 (and_2_out, E_ADD, ADD);
  ALU_1bit alu_1bit_1 (
    .ACi(AC[0]), .DRi(DR_2[0]), .AND(AND), .ADD(ADD), .DR(DR), .COM(COM), .ACi_1(AC[1]), .SHR(CIR),
    .ACi_1_2(E), .SHL(CIL), .ACi_2(AC_2[0]), .E(C0), .Cin(1'b0));
  ALU_1bit alu_1bit_2 (
    .ACi(AC[1]), .DRi(DR_2[1]), .AND(AND), .ADD(ADD), .DR(DR), .COM(COM), .ACi_1(AC[2]), .SHR(CIR),
    .ACi_1_2(AC[0]), .SHL(CIL), .ACi_2(AC_2[1]), .E(C1), .Cin(C0));
  ALU_1bit alu_1bit_3 (
    .ACi(AC[2]), .DRi(DR_2[2]), .AND(AND), .ADD(ADD), .DR(DR), .COM(COM), .ACi_1(AC[3]), .SHR(CIR),
    .ACi_1_2(AC[1]), .SHL(CIL), .ACi_2(AC_2[2]), .E(C2), .Cin(C1));
  and and_3 (and_3_out, AC[0], CIL);
  ALU_1bit alu_1bit_4 (
    .ACi(AC[3]), .DRi(DR_2[3]), .AND(AND), .ADD(ADD), .DR(DR), .COM(COM), .ACi_1(AC[3]), .SHR(CIR),
    .ACi_1_2(AC[2]), .SHL(CIL), .ACi_2(AC_2[3]), .E(C3), .Cin(C2));
  ALU_1bit alu_1bit_5 (
    .ACi(AC[4]), .DRi(DR_2[4]), .AND(AND), .ADD(ADD), .DR(DR), .COM(COM), .ACi_1(AC[5]), .SHR(CIR),
    .ACi_1_2(AC[3]), .SHL(CIL), .ACi_2(AC_2[4]), .E(C4), .Cin(C3));
  ALU_1bit alu_1bit_6 (
    .ACi(AC[5]), .DRi(DR_2[5]), .AND(AND), .ADD(ADD), .DR(DR), .COM(COM), .ACi_1(AC[6]), .SHR(CIR),
    .ACi_1_2(AC[4]), .SHL(CIL), .ACi_2(AC_2[5]), .E(C5), .Cin(C4));
  ALU_1bit alu_1bit_7 (
    .ACi(AC[6]), .DRi(DR_2[6]), .AND(AND), .ADD(ADD), .DR(DR), .COM(COM), .ACi_1(AC[7]), .SHR(CIR),
    .ACi_1_2(AC[5]), .SHL(CIL), .ACi_2(AC_2[6]), .E(C6), .Cin(C5));
  ALU_1bit alu_1bit_8 (
    .ACi(AC[7]), .DRi(DR_2[7]), .AND(AND), .ADD(ADD), .DR(DR), .COM(COM), .ACi_1(AC[8]), .SHR(CIR),
    .ACi_1_2(AC[6]), .SHL(CIL), .ACi_2(AC_2[7]), .E(C7), .Cin(C6));
  ALU_1bit alu_1bit_9 (
    .ACi(AC[8]), .DRi(DR_2[8]), .AND(AND), .ADD(ADD), .DR(DR), .COM(COM), .ACi_1(AC[9]), .SHR(CIR),
    .ACi_1_2(AC[7]), .SHL(CIL), .ACi_2(AC_2[8]), .E(C8), .Cin(C7));
  ALU_1bit alu_1bit_10 (
    .ACi(AC[9]), .DRi(DR_2[9]), .AND(AND), .ADD(ADD), .DR(DR), .COM(COM), .ACi_1(AC[10]), .SHR(CIR),
    .ACi_1_2(AC[8]), .SHL(CIL), .ACi_2(AC_2[9]), .E(C9), .Cin(C8));
  ALU_1bit alu_1bit_11 (
    .ACi(AC[10]), .DRi(DR_2[10]), .AND(AND), .ADD(ADD), .DR(DR), .COM(COM), .ACi_1(AC[11]), .SHR(CIR),
    .ACi_1_2(AC[9]), .SHL(CIL), .ACi_2(AC_2[10]), .E(C10), .Cin(C9));
  ALU_1bit alu_1bit_12 (
    .ACi(AC[11]), .DRi(DR_2[11]), .AND(AND), .ADD(ADD), .DR(DR), .COM(COM), .ACi_1(AC[12]), .SHR(CIR),
    .ACi_1_2(AC[10]), .SHL(CIL), .ACi_2(AC_2[11]), .E(C11), .Cin(C10));
  ALU_1bit alu_1bit_13 (
    .ACi(AC[12]), .DRi(DR_2[12]), .AND(AND), .ADD(ADD), .DR(DR), .COM(COM), .ACi_1(AC[13]), .SHR(CIR),
    .ACi_1_2(AC[11]), .SHL(CIL), .ACi_2(AC_2[12]), .E(C12), .Cin(C11));
  ALU_1bit alu_1bit_14 (
    .ACi(AC[13]), .DRi(DR_2[13]), .AND(AND), .ADD(ADD), .DR(DR), .COM(COM), .ACi_1(AC[14]), .SHR(CIR),
    .ACi_1_2(AC[12]), .SHL(CIL), .ACi_2(AC_2[13]), .E(C13), .Cin(C12));
  ALU_1bit alu_1bit_15 (
    .ACi(AC[14]), .DRi(DR_2[14]), .AND(AND), .ADD(ADD), .DR(DR), .COM(COM), .ACi_1(AC[15]), .SHR(CIR),
    .ACi_1_2(AC[13]), .SHL(CIL), .ACi_2(AC_2[14]), .E(C14), .Cin(C13));
  ALU_1bit alu_1bit_16 (
    .ACi(AC[15]), .DRi(DR_2[15]), .AND(AND), .ADD(ADD), .DR(DR), .COM(COM), .ACi_1(E), .SHR(CIR),
    .ACi_1_2(AC[14]), .SHL(CIL), .ACi_2(AC_2[15]), .E(E_ADD), .Cin(C14));
  or or_1 (E_2, and_1_out, and_2_out, and_3_out);

  // Other names for the same wires on the sheet: A = AND; E_SHL = AC[0]; E_SHR = AC[15]; B = ADD; C = DR; D = COM;
  //   DR0 = DR_2[0]; DR1 = DR_2[1]; DR2 = DR_2[2]; DR3 = DR_2[3]; DR4 = DR_2[4]; DR5 = DR_2[5]; DR6 = DR_2[6];
  //   DR7 = DR_2[7]; DR8 = DR_2[8]; DR9 = DR_2[9]; DR10 = DR_2[10]; DR11 = DR_2[11]; DR12 = DR_2[12]; DR13 = DR_2[13];
  //   DR14 = DR_2[14]; DR15 = DR_2[15]; E_carry_bit = E; E_t = CIR; F = CIL

  // Notes on the sheet:
  //   CIL
  //   CIR
  //   Serial in
  //   Bit 0
  //   Bit 1
  //   Bit 2
  //   Serial in
endmodule

// ALU
module ALU_1bit (
  input  ACi,
  input  DRi,
  input  AND,
  input  Cin,
  input  ADD,
  input  DR,
  input  COM,
  input  ACi_1,
  input  SHR,
  input  ACi_1_2,
  input  SHL,
  output ACi_2,
  output E
);

  wire adder_1_out, and_1_out, and_2_out, and_3_out, and_4_out, and_5_out, and_6_out, not_1_out;

  not not_1 (not_1_out, ACi);
  Adder #(.width(1)) adder_1 (.a(ACi), .b(DRi), .out(adder_1_out), .cin(Cin), .cout(E));
  and and_1 (and_1_out, DRi, DR);
  and and_2 (and_2_out, not_1_out, COM);
  and and_3 (and_3_out, ACi_1_2, SHL);
  and and_4 (and_4_out, ACi, DRi, AND);
  and and_5 (and_5_out, adder_1_out, ADD);
  and and_6 (and_6_out, ACi_1, SHR);
  or or_1 (ACi_2, and_4_out, and_5_out, and_1_out, and_2_out, and_6_out, and_3_out);
endmodule

module BUS (
  input  Write,
  input  Read,
  input  LDAR,
  input  INAR,
  input  CLRAR,
  input  LDPC,
  input  INPC,
  input  CLRPC,
  input  LDDR,
  input  INDR,
  input  CLRDR,
  input  LDAC,
  input  INAC,
  input  CIL,
  input  CIR,
  input  CLRAC,
  input  ADD,
  input  DR,
  input  COM,
  input  AND,
  input  LDIR,
  input  LDTR,
  input  INTR,
  input  CLRTR
);

  wire alu_combined_1_e_2, clk, E_q;
  wire [2:0] BUSSEL;
  wire [11:0] AR_q, bit_extender_1_out, bit_extender_2_out, PC_q;
  wire [15:0] alu_combined_1_ac_2, bit_extender_3_out, bit_extender_4_out, counter_2_q, DR_t, IR_q, M,
       multiplexer_1_out, TR_q;

  Clock clock_1 (.out(clk));
  ALU_Combined alu_combined_1 (
    .AC(counter_2_q), .DR_2(DR_t), .AC_2(alu_combined_1_ac_2), .E_2(alu_combined_1_e_2), .ADD(ADD), .DR(DR),
    .E(E_q), .AND(AND), .COM(COM), .CIR(CIR), .CIL(CIL));
  Bit_Extender #(.in_width(16), .out_width(12)) bit_extender_1 (.in(multiplexer_1_out), .out(bit_extender_1_out));
  Bit_Extender #(.in_width(16), .out_width(12)) bit_extender_2 (.in(multiplexer_1_out), .out(bit_extender_2_out));
  D_Flip_Flop E (.clk(clk), .D(alu_combined_1_e_2), .Q(E_q), .preset(1'b0), .en(1'b1), .reset(1'b0));  // open: Qn
  Counter #(.width(12), .max('hfff)) AR (
    .load(LDAR), .D(bit_extender_1_out), .count(INAR), .Q(AR_q), .clk(clk), .clr(CLRAR));  // open: carry
  Counter #(.width(12), .max('hfff)) PC (
    .load(LDPC), .D(bit_extender_2_out), .count(INPC), .Q(PC_q), .clk(clk), .clr(CLRPC));  // open: carry
  Counter #(.width(16), .max('hffff)) counter_1 (
    .load(LDDR), .D(multiplexer_1_out), .count(INDR), .Q(DR_t), .clk(clk), .clr(CLRDR));  // open: carry
  Counter #(.width(16), .max('hffff)) counter_2 (
    .load(LDAC), .D(alu_combined_1_ac_2), .count(INAC), .Q(counter_2_q), .clk(clk), .clr(CLRAC));  // open: carry
  Counter #(.width(16), .max('hffff)) IR (
    .load(LDIR), .D(multiplexer_1_out), .count(1'b0), .Q(IR_q), .clk(clk), .clr(1'b0));  // open: carry
  Counter #(.width(16), .max('hffff)) TR (
    .load(LDTR), .D(multiplexer_1_out), .count(INTR), .Q(TR_q), .clk(clk), .clr(CLRTR));  // open: carry
  RAM #(.addrWidth(12), .dataWidth(16), .bus("separate")) ram_1 (
    .addr(AR_q), .din(multiplexer_1_out), .data(M), .str(Write), .sel(1'b1), .clk(clk), .ld(Read), .clr(1'b0));
  assign bit_extender_3_out = {{4{1'b0}}, AR_q};  // Bit_Extender bit_extender_3
  assign bit_extender_4_out = {{4{1'b0}}, PC_q};  // Bit_Extender bit_extender_4
  Multiplexer #(.select(3), .width(16), .enable("false")) multiplexer_1 (
    .in1(bit_extender_3_out), .in2(bit_extender_4_out), .in3(DR_t), .in4(counter_2_q), .in5(IR_q),
    .in6(TR_q), .in7(M), .out(multiplexer_1_out), .sel(BUSSEL));  // open: in0

  // Notes on the sheet:
  //   MEM
  //   DR
  //   AC
endmodule
