// Logisim project Milestone1_mux_17610.circ as structural Verilog
module ALU (
  input  [15:0] AC,
  input  [15:0] DR,
  input  AND,
  input  COM,
  input  ADD,
  input  Transfer_DR,
  input  CIL,
  input  CIR,
  output [15:0] AC_2,
  output V,
  output E
);

  wire bitselector_1_out, bitselector_2_out;
  wire [3:0] priority_encoder_1_out;
  wire [15:0] adder_1_out, adder_2_out, AND_out, NOT_out, OR_out, shifter_1_out, shifter_2_out,
       shifter_3_out, shifter_4_out, shifter_5_out, shifter_6_out, subtractor_1_out, subtractor_2_out,
       XOR_out;

  assign AND_out = AC & DR;  // AND_Gate AND, 16 bits wide
  assign OR_out = AC | DR;  // OR_Gate OR, 16 bits wide
  assign XOR_out = AC ^ DR;  // XOR_Gate XOR, 16 bits wide
  assign NOT_out = ~AC;  // NOT_Gate NOT, 16 bits wide
  Shifter #(.width(16)) shifter_1 (.in(AC), .\dist (4'b0001), .out(shifter_1_out));
  Shifter #(.width(16), .shift("lr")) shifter_2 (.in(AC), .\dist (4'b0001), .out(shifter_2_out));
  Shifter #(.width(16), .shift("rl")) shifter_3 (.in(AC), .\dist (4'b0001), .out(shifter_3_out));
  Shifter #(.width(16), .shift("rr")) shifter_4 (.in(AC), .\dist (4'b0001), .out(shifter_4_out));
  BitSelector #(.width(16)) bitselector_1 (.in(AC), .out(bitselector_1_out), .sel(4'b1111));
  BitSelector #(.width(16)) bitselector_2 (.in(AC), .out(bitselector_2_out), .sel(4'b1110));
  Shifter #(.width(16)) shifter_5 (.in(AC), .\dist (4'b0001), .out(shifter_5_out));
  Shifter #(.width(16), .shift("ar")) shifter_6 (.in(AC), .\dist (4'b0001), .out(shifter_6_out));
  Adder #(.width(16)) adder_1 (.a(AC), .b(DR), .out(adder_1_out), .cin(1'b0), .cout(E));
  Subtractor #(.width(16)) subtractor_1 (.a(AC), .b(DR), .out(subtractor_1_out), .bin(1'b0));  // open: bout
  Adder #(.width(16)) adder_2 (.a(AC), .b(16'h1), .out(adder_2_out), .cin(1'b0));  // open: cout
  Subtractor #(.width(16)) subtractor_2 (.a(AC), .b(16'h1), .out(subtractor_2_out), .bin(1'b0));  // open: bout
  xor xor_2 (V, bitselector_1_out, bitselector_2_out);
  Multiplexer #(.select(4), .width(16), .enable("false")) multiplexer_1 (
    .in0(AND_out), .in1(OR_out), .in2(XOR_out), .in3(NOT_out), .in4(shifter_1_out), .in5(shifter_2_out),
    .in6(shifter_3_out), .in7(shifter_4_out), .in8(shifter_5_out), .in9(shifter_6_out), .in10(adder_1_out),
    .in11(subtractor_1_out), .in12(adder_2_out), .in13(subtractor_2_out), .in14(AC), .in15(DR), .out(AC_2),
    .sel(priority_encoder_1_out));
  Priority_Encoder #(.select(4)) priority_encoder_1 (
    .in0(AND), .in1(1'b0), .in2(1'b0), .in3(COM), .in4(1'b0), .in5(1'b0), .in6(CIL), .in7(CIR), .in8(1'b0),
    .in9(1'b0), .in10(ADD), .in11(1'b0), .in12(1'b0), .in13(1'b0), .in14(1'b0), .in15(Transfer_DR),
    .out(priority_encoder_1_out));

  // Other names for the same wires on the sheet: c_add = E

  // Notes on the sheet:
  //   LSL
  //   LSR
  //   CSL
  //   CSR
  //   ASL
  //   ASR
  //   ADD
  //   SUB
  //   INC
  //   DEC
  //   Transfer AC
  //   Transfer DR
  //   Over Flow of ASL
  //   The role of the encoder is to 
  //   convert the control signals to selection lines
  //   so, in the process, the arithmetic/ logical/ shift operations
  //   that are not present inside the BC ALU
  //   were replaced witha constant signal of 0
  //   since they can never be selected
endmodule

module BUS (
  input  write,
  input  read,
  input  LDAR,
  input  INAR,
  input  CLRAR,
  input  LDPC,
  input  INPC,
  input  CLRPC,
  input  [2:0] BUS_SEL,
  input  LDDR,
  input  INDR,
  input  CLRDR,
  input  LDAC,
  input  AND,
  input  INAC,
  input  CLRAC,
  input  CIL,
  input  DR,
  input  COM,
  input  CIR,
  input  ADD,
  input  LDIR,
  input  LDTR,
  input  INTR,
  input  CLRTR
);

  wire alu_1_e, clk;
  wire [11:0] AR_q, bit_extender_1_out, bit_extender_2_out, PC_q;
  wire [15:0] alu_1_ac_2, bit_extender_3_out, bit_extender_4_out, counter_1_q, counter_2_q, IR_q, M,
       multiplexer_1_out, TR_q;

  Clock clock_1 (.out(clk));
  ALU alu_1 (
    .AC(counter_2_q), .DR(counter_1_q), .AC_2(alu_1_ac_2), .E(alu_1_e), .AND(AND), .COM(COM), .CIR(CIR),
    .ADD(ADD), .Transfer_DR(DR), .CIL(CIL));  // open: V
  Bit_Extender #(.in_width(16), .out_width(12)) bit_extender_1 (.in(multiplexer_1_out), .out(bit_extender_1_out));
  Bit_Extender #(.in_width(16), .out_width(12)) bit_extender_2 (.in(multiplexer_1_out), .out(bit_extender_2_out));
  D_Flip_Flop E (.clk(clk), .D(alu_1_e), .preset(1'b0), .en(1'b1), .reset(1'b0));  // open: Q, Qn
  Counter #(.width(12), .max('hfff)) AR (
    .load(LDAR), .D(bit_extender_1_out), .count(INAR), .Q(AR_q), .clk(clk), .clr(CLRAR));  // open: carry
  Counter #(.width(12), .max('hfff)) PC (
    .load(LDPC), .D(bit_extender_2_out), .count(INPC), .Q(PC_q), .clk(clk), .clr(CLRPC));  // open: carry
  Counter #(.width(16), .max('hffff)) counter_1 (
    .load(LDDR), .D(multiplexer_1_out), .count(INDR), .Q(counter_1_q), .clk(clk), .clr(CLRDR));  // open: carry
  Counter #(.width(16), .max('hffff)) counter_2 (
    .load(LDAC), .D(alu_1_ac_2), .count(INAC), .Q(counter_2_q), .clk(clk), .clr(CLRAC));  // open: carry
  Counter #(.width(16), .max('hffff)) IR (
    .load(LDIR), .D(multiplexer_1_out), .count(1'b0), .Q(IR_q), .clk(clk), .clr(1'b0));  // open: carry
  Counter #(.width(16), .max('hffff)) TR (
    .load(LDTR), .D(multiplexer_1_out), .count(INTR), .Q(TR_q), .clk(clk), .clr(CLRTR));  // open: carry
  RAM #(.addrWidth(12), .dataWidth(16), .bus("separate")) ram_1 (
    .addr(AR_q), .din(multiplexer_1_out), .data(M), .str(write), .sel(1'b1), .clk(clk), .ld(read), .clr(1'b0));
  assign bit_extender_3_out = {{4{1'b0}}, AR_q};  // Bit_Extender bit_extender_3
  assign bit_extender_4_out = {{4{1'b0}}, PC_q};  // Bit_Extender bit_extender_4
  Multiplexer #(.select(3), .width(16), .enable("false")) multiplexer_1 (
    .in1(bit_extender_3_out), .in2(bit_extender_4_out), .in3(counter_1_q), .in4(counter_2_q), .in5(IR_q),
    .in6(TR_q), .in7(M), .out(multiplexer_1_out), .sel(BUS_SEL));  // open: in0

  // Notes on the sheet:
  //   MEM
  //   DR
  //   AC
endmodule
