// Logisim project Submission 1.circ as structural Verilog: 1 circuit, main circuit main
module main (
  input  L1,
  input  INC1,
  input  CLR1,
  input  L2,
  input  INC2,
  input  CLR2,
  input  L3,
  input  INC3,
  input  CLR3,
  input  [1:0] S,
  input  E,
  input  L4,
  input  INC4,
  input  CLR4
);

  wire clock_1_out;
  wire [15:0] multiplexer_1_out, R0_q, R1_q, R2_q, R3_q;

  Clock clock_1 (.out(clock_1_out));
  Counter #(.width(16), .max('hffff)) R0 (
    .load(L1), .D(multiplexer_1_out), .count(INC1), .Q(R0_q), .clk(clock_1_out), .clr(CLR1));  // open: carry
  Counter #(.width(16), .max('hffff)) R1 (
    .load(L2), .D(multiplexer_1_out), .count(INC2), .Q(R1_q), .clk(clock_1_out), .clr(CLR2));  // open: carry
  Counter #(.width(16), .max('hffff)) R2 (
    .load(L3), .D(multiplexer_1_out), .count(INC3), .Q(R2_q), .clk(clock_1_out), .clr(CLR3));  // open: carry
  Counter #(.width(16), .max('hffff)) R3 (
    .load(L4), .D(multiplexer_1_out), .count(INC4), .Q(R3_q), .clk(clock_1_out), .clr(CLR4));  // open: carry
  Multiplexer #(.select(2), .width(16)) multiplexer_1 (
    .in0(R0_q), .in1(R1_q), .in2(R2_q), .in3(R3_q), .out(multiplexer_1_out), .sel(S), .en(E));
endmodule
