// Logisim project Submission 2.circ as structural Verilog: 1 circuit, main circuit main
module main (
  input  in_1,
  input  in_2,
  input  in_3,
  input  in_4,
  input  [2:0] in_5,
  input  in_6,
  input  [2:0] in_7,
  input  in_8,
  input  [2:0] in_9,
  input  in_10,
  input  [2:0] in_11,
  input  E,
  input  [3:0] S,
  input  [2:0] in_14,
  input  [2:0] in_15,
  input  in_16,
  input  [7:0] in_17,
  input  [7:0] in_18,
  output [7:0] out_19
);

  wire clock_1_out;
  wire [7:0] A_q, adder_1_out, adder_2_out, and_1_out, B_q, multiplexer_1_out, not_1_out, or_1_out,
       shifter_1_out, shifter_2_out, shifter_3_out, shifter_4_out, shifter_5_out, shifter_6_out,
       subtractor_1_out, subtractor_2_out, xor_1_out;

  Counter A (.load(in_2), .count(in_3), .Q(A_q), .clk(clock_1_out));  // open: D, carry, clr
  Clock clock_1 (.out(clock_1_out));
  Counter B (.load(in_1), .count(in_4), .Q(B_q), .clk(clock_1_out));  // open: D, carry, clr
  assign and_1_out = A_q & B_q;  // AND_Gate and_1, 8 bits wide
  assign or_1_out = A_q | B_q;  // OR_Gate or_1, 8 bits wide
  assign xor_1_out = A_q ^ B_q;  // XOR_Gate xor_1, 8 bits wide
  assign not_1_out = ~A_q;  // NOT_Gate not_1, 8 bits wide
  Shifter shifter_1 (.in(A_q), .\dist (in_5), .out(shifter_1_out));
  Shifter #(.shift("lr")) shifter_2 (.in(A_q), .\dist (in_7), .out(shifter_2_out));
  Shifter #(.shift("rl")) shifter_3 (.in(A_q), .\dist (in_9), .out(shifter_3_out));
  Shifter #(.shift("rr")) shifter_4 (.in(A_q), .\dist (in_11), .out(shifter_4_out));
  Shifter #(.shift("ar")) shifter_5 (.in(A_q), .\dist (in_14), .out(shifter_5_out));
  Shifter #(.shift("ar")) shifter_6 (.in(A_q), .\dist (in_15), .out(shifter_6_out));
  Adder adder_1 (.a(A_q), .b(B_q), .out(adder_1_out));  // open: cin, cout
  Subtractor subtractor_1 (.a(A_q), .b(B_q), .out(subtractor_1_out));  // open: bin, bout
  Adder adder_2 (.a(A_q), .b(in_17), .out(adder_2_out), .cin(in_16));  // open: cout
  Subtractor subtractor_2 (.a(A_q), .b(in_18), .out(subtractor_2_out), .bin(in_16));  // open: bout
  Multiplexer #(.select(4), .width(8)) multiplexer_1 (
    .in0(and_1_out), .in1(or_1_out), .in2(xor_1_out), .in3(not_1_out), .in4(shifter_1_out),
    .in5(shifter_2_out), .in6(shifter_3_out), .in7(shifter_4_out), .in8(shifter_5_out), .in9(shifter_6_out),
    .in10(adder_1_out), .in11(subtractor_1_out), .in12(adder_2_out), .in13(subtractor_2_out), .in14(A_q),
    .in15(B_q), .out(multiplexer_1_out), .sel(S), .en(E));
  Counter C (
    .load(in_6), .D(multiplexer_1_out), .count(in_8), .Q(out_19), .clk(clock_1_out), .clr(in_10));  // open: carry
endmodule
