// Logisim project T17 31-1543 S2.circ as structural Verilog: 1 circuit, main circuit main
module main (
  input  [15:0] in_1,
  input  [15:0] in_2,
  input  [3:0] S,
  output [15:0] out_4,
  output E
);

  wire adder_1_cout, adder_2_cout, subtractor_1_bout, subtractor_2_bout, xor_1_out;
  wire [15:0] adder_1_out, adder_2_out, and_1_out, not_1_out, or_2_out, shifter_1_out, shifter_2_out,
       shifter_3_out, shifter_4_out, shifter_5_out, shifter_6_out, subtractor_1_out, subtractor_2_out,
       xor_2_out;

  xor xor_1 (xor_1_out, in_2[15], in_2[14]);
  or or_1 (E, adder_2_cout, adder_1_cout, xor_1_out, subtractor_1_bout, subtractor_2_bout);
  assign and_1_out = in_2 & in_1;  // AND_Gate and_1, 16 bits wide
  assign or_2_out = in_2 | in_1;  // OR_Gate or_2, 16 bits wide
  assign xor_2_out = in_2 ^ in_1;  // XOR_Gate xor_2, 16 bits wide
  assign not_1_out = ~in_2;  // NOT_Gate not_1, 16 bits wide
  Shifter #(.width(16)) shifter_1 (.in(in_2), .\dist (4'b0001), .out(shifter_1_out));
  Shifter #(.width(16), .shift("lr")) shifter_2 (.in(in_2), .\dist (4'b0001), .out(shifter_2_out));
  Shifter #(.width(16), .shift("rl")) shifter_3 (.in(in_2), .\dist (4'b0001), .out(shifter_3_out));
  Shifter #(.width(16), .shift("rr")) shifter_4 (.in(in_2), .\dist (4'b0001), .out(shifter_4_out));
  Shifter #(.width(16)) shifter_5 (.in(in_2), .\dist (4'b0001), .out(shifter_5_out));
  Shifter #(.width(16), .shift("ar")) shifter_6 (.in(in_2), .\dist (4'b0001), .out(shifter_6_out));
  Adder #(.width(16)) adder_1 (.a(in_2), .b(in_1), .out(adder_1_out), .cout(adder_1_cout));  // open: cin
  Subtractor #(.width(16)) subtractor_1 (
    .a(in_2), .b(in_1), .out(subtractor_1_out), .bout(subtractor_1_bout));  // open: bin
  Adder #(.width(16)) adder_2 (.a(in_2), .b({16{1'b0}}), .out(adder_2_out), .cin(1'b1), .cout(adder_2_cout));
  Subtractor #(.width(16)) subtractor_2 (
    .a(in_2), .b({16{1'b0}}), .out(subtractor_2_out), .bin(1'b1), .bout(subtractor_2_bout));
  Multiplexer #(.select(4), .width(16), .enable("false")) multiplexer_1 (
    .in0(and_1_out), .in1(or_2_out), .in2(xor_2_out), .in3(not_1_out), .in4(shifter_1_out),
    .in5(shifter_2_out), .in6(shifter_3_out), .in7(shifter_4_out), .in8(shifter_5_out), .in9(shifter_6_out),
    .in10(adder_1_out), .in11(subtractor_1_out), .in12(adder_2_out), .in13(subtractor_2_out), .in14(in_2),
    .in15(in_1), .out(out_4), .sel(S));
endmodule
