// Logisim project T17 31-1543 S3.circ as structural Verilog: 1 circuit, main circuit main
module main (
  input  INC,
  input  CLR
);

  wire clock_1_out, decoder_1_out2, decoder_1_out3, decoder_1_out4, decoder_1_out5, decoder_1_out6,
       decoder_1_out7, decoder_2_out0, decoder_2_out1, decoder_2_out2, decoder_2_out3, decoder_2_out4,
       decoder_2_out5, decoder_2_out6, decoder_2_out7, decoder_2_out8, decoder_2_out9, decoder_2_out10,
       decoder_2_out11, decoder_2_out12, decoder_2_out13, decoder_2_out14, decoder_2_out15, I_p3, I_p4;
  wire [3:0] SC_q;
  wire [15:0] IR_q;

  Clock clock_1 (.out(clock_1_out));
  Counter #(.width(16), .max('hffff)) IR (.Q(IR_q), .clk(clock_1_out));  // open: load, D, count, carry, clr
  Counter #(.width(4), .max('hf)) SC (.count(INC), .Q(SC_q), .clk(clock_1_out), .clr(CLR));  // open: load, D, carry
  // D_Flip_Flop I: pin names not known; wires that end beside it: clock_1_out, IR_q[15], I_p3, I_p4
  Decoder #(.select(3), .enable("false")) decoder_1 (
    .out0(I_p3), .out1(I_p4), .out2(decoder_1_out2), .out3(decoder_1_out3), .out4(decoder_1_out4),
    .out5(decoder_1_out5), .out6(decoder_1_out6), .out7(decoder_1_out7), .sel(IR_q[14:12]));
  Decoder #(.select(4), .enable("false")) decoder_2 (
    .out0(decoder_2_out0), .out1(decoder_2_out1), .out2(decoder_2_out2), .out3(decoder_2_out3),
    .out4(decoder_2_out4), .out5(decoder_2_out5), .out6(decoder_2_out6), .out7(decoder_2_out7),
    .out8(decoder_2_out8), .out9(decoder_2_out9), .out10(decoder_2_out10), .out11(decoder_2_out11),
    .out12(decoder_2_out12), .out13(decoder_2_out13), .out14(decoder_2_out14), .out15(decoder_2_out15),
    .sel(SC_q));
endmodule
