// Logisim project T17 31-1543,31-2000 M2.circ as structural Verilog: 3 circuits, main circuit main
module main (
  input  CLK,
  input  [15:0] IR,
  input  [15:0] DR,
  output LDAC,
  output CLAC,
  output [2:0] BUS,
  output WRITE,
  output READ,
  output LDPC,
  output LDAR,
  output LDDR,
  output LDIR,
  output TransferDR,
  output ADD,
  output PCINC
);

  wire and_1_out, and_2_out, and_3_out, and_4_out, and_5_out, and_6_out, and_10_out, and_11_out, and_12_out,
       and_13_out, and_14_out, and_15_out, and_16_out, and_17_out, and_18_out, and_19_out, D0, D1, D2, D3,
       D4, D5, D6, D7, I, nand_1_out, not_1_out, not_2_out, not_3_out, not_4_out, not_5_out, not_6_out,
       not_7_out, or_1_out, or_2_out, or_3_out, or_4_out, S_q, T0, T2, T3, T4, T5, T6, T7, T8, T9, T10, T11,
       T12, T13, T14, T15, X1, X3, X4;
  wire [3:0] SC_q;

  and and_1 (and_1_out, D4, T4);
  not not_1 (not_1_out, I);
  Counter #(.width(4), .max('hf)) SC (.count(S_q), .Q(SC_q), .clk(CLK), .clr(or_1_out));  // open: load, D, carry
  or or_1 (or_1_out, and_1_out, and_3_out, and_2_out, and_5_out, and_4_out, and_6_out);
  and and_2 (and_2_out, D2, T5);
  and and_3 (and_3_out, D3, T4);
  D_Flip_Flop S (.clk(CLK), .D(nand_1_out), .Q(S_q));  // open: Qn, preset, en, reset
  nand nand_1 (nand_1_out, D7, not_1_out, T3, IR[0]);
  and and_4 (and_4_out, D6, T6);
  and and_5 (and_5_out, D1, T5);
  D_Flip_Flop u_I (.clk(CLK), .D(IR[15]), .Q(I));  // open: Qn, preset, en, reset
  Decoder #(.select(3), .enable("false")) decoder_1 (
    .out0(D0), .out1(D1), .out2(D2), .out3(D3), .out4(D4), .out5(D5), .out6(D6), .out7(D7), .sel(IR[14:12]));
  Decoder #(.select(4), .enable("false")) decoder_2 (
    .out0(T0), .out1(LDIR), .out2(T2), .out3(T3), .out4(T4), .out5(T5), .out6(T6), .out7(T7), .out8(T8),
    .out9(T9), .out10(T10), .out11(T11), .out12(T12), .out13(T13), .out14(T14), .out15(T15), .sel(SC_q));
  and and_6 (and_6_out, D7, not_2_out, T3, not_3_out);
  not not_2 (not_2_out, I);
  not not_3 (not_3_out, or_2_out);
  or or_2 (or_2_out, DR[0], DR[1], DR[2], DR[3], DR[4], DR[5], DR[6], DR[7], DR[8], DR[9], DR[10], DR[11], DR[12], DR[13], DR[14], DR[15]);
  not not_4 (not_4_out, I);
  and and_7 (LDPC, D4, T4);
  not not_5 (not_5_out, I);
  not not_6 (not_6_out, D7);
  not not_7 (not_7_out, D7);
  and and_8 (TransferDR, T5, D2);
  and and_9 (ADD, T5, D1);
  and and_10 (and_10_out, not_3_out, D7, not_4_out, T3);
  and and_11 (and_11_out, D1, T5);
  and and_12 (and_12_out, T5, D2);
  and and_13 (and_13_out, D3, T4);
  and and_14 (and_14_out, D6, T6);
  and and_15 (and_15_out, not_6_out, I, T3);
  and and_16 (and_16_out, T4, or_3_out);
  or or_3 (or_3_out, D0, D1, D2, D6);
  and and_17 (and_17_out, not_7_out, I, T3);
  and and_18 (and_18_out, T4, or_4_out);
  or or_4 (or_4_out, D1, D6);
  and and_19 (and_19_out, D6, T5);
  or or_5 (PCINC, and_10_out, LDIR);
  or or_6 (LDAC, and_11_out, and_12_out);
  and and_20 (CLAC, D7, not_5_out, T3, IR[11]);
  or or_7 (WRITE, and_13_out, and_14_out);
  or or_8 (READ, LDIR, and_15_out, and_16_out);
  or or_9 (LDAR, and_17_out, T0);
  or or_10 (LDDR, and_18_out, and_19_out);
  and and_21 (X4, D3, T4);
  and and_22 (X1, D4, T4);
  and and_23 (X3, D6, T6);
  Priority_Encoder priority_encoder_1 (
    .in1(X1), .in2(T0), .in3(X3), .in4(X4), .in5(1'b0), .in6(1'b0), .in7(READ), .out(BUS), .en_in(1'b1));  // open: in0, gs, en_out

  // Other names for the same wires on the sheet: T1 = LDIR; X2 = T0

  // Notes on the sheet:
  //   This circuit is the control Unit and it is attached to The Bus in the Bus circuit
endmodule

module ALU (
  input  [15:0] AC,
  input  [15:0] DR,
  input  AND,
  input  COM,
  input  ADD,
  input  Transfer_DR,
  input  CIL,
  input  CIR,
  output [15:0] AC_2,
  output V,
  output E
);

  wire bitselector_1_out, bitselector_2_out;
  wire [3:0] priority_encoder_1_out;
  wire [15:0] adder_1_out, adder_2_out, AND_out, NOT_out, OR_out, shifter_1_out, shifter_2_out,
       shifter_3_out, shifter_4_out, shifter_5_out, shifter_6_out, subtractor_1_out, subtractor_2_out,
       XOR_out;

  assign AND_out = AC & DR;  // AND_Gate AND, 16 bits wide
  assign OR_out = AC | DR;  // OR_Gate OR, 16 bits wide
  assign XOR_out = AC ^ DR;  // XOR_Gate XOR, 16 bits wide
  assign NOT_out = ~AC;  // NOT_Gate NOT, 16 bits wide
  Shifter #(.width(16)) shifter_1 (.in(AC), .\dist (4'b0001), .out(shifter_1_out));
  Shifter #(.width(16), .shift("lr")) shifter_2 (.in(AC), .\dist (4'b0001), .out(shifter_2_out));
  Shifter #(.width(16), .shift("rl")) shifter_3 (.in(AC), .\dist (4'b0001), .out(shifter_3_out));
  Shifter #(.width(16), .shift("rr")) shifter_4 (.in(AC), .\dist (4'b0001), .out(shifter_4_out));
  BitSelector #(.width(16)) bitselector_1 (.in(AC), .out(bitselector_1_out), .sel(4'b1111));
  BitSelector #(.width(16)) bitselector_2 (.in(AC), .out(bitselector_2_out), .sel(4'b1110));
  Shifter #(.width(16)) shifter_5 (.in(AC), .\dist (4'b0001), .out(shifter_5_out));
  Shifter #(.width(16), .shift("ar")) shifter_6 (.in(AC), .\dist (4'b0001), .out(shifter_6_out));
  Adder #(.width(16)) adder_1 (.a(AC), .b(DR), .out(adder_1_out), .cin(1'b0), .cout(E));
  Subtractor #(.width(16)) subtractor_1 (.a(AC), .b(DR), .out(subtractor_1_out), .bin(1'b0));  // open: bout
  Adder #(.width(16)) adder_2 (.a(AC), .b(16'h1), .out(adder_2_out), .cin(1'b0));  // open: cout
  Subtractor #(.width(16)) subtractor_2 (.a(AC), .b(16'h1), .out(subtractor_2_out), .bin(1'b0));  // open: bout
  xor xor_2 (V, bitselector_1_out, bitselector_2_out);
  Multiplexer #(.select(4), .width(16), .enable("false")) multiplexer_1 (
    .in0(AND_out), .in1(OR_out), .in2(XOR_out), .in3(NOT_out), .in4(shifter_1_out), .in5(shifter_2_out),
    .in6(shifter_3_out), .in7(shifter_4_out), .in8(shifter_5_out), .in9(shifter_6_out), .in10(adder_1_out),
    .in11(subtractor_1_out), .in12(adder_2_out), .in13(subtractor_2_out), .in14(AC), .in15(DR), .out(AC_2),
    .sel(priority_encoder_1_out));
  Priority_Encoder #(.select(4)) priority_encoder_1 (
    .in0(AND), .in1(1'b0), .in2(1'b0), .in3(COM), .in4(1'b0), .in5(1'b0), .in6(CIL), .in7(CIR), .in8(1'b0),
    .in9(1'b0), .in10(ADD), .in11(1'b0), .in12(1'b0), .in13(1'b0), .in14(1'b0), .in15(Transfer_DR),
    .out(priority_encoder_1_out));

  // Other names for the same wires on the sheet: c_add = E

  // Notes on the sheet:
  //   LSL
  //   LSR
  //   CSL
  //   CSR
  //   ASL
  //   ASR
  //   ADD
  //   SUB
  //   INC
  //   DEC
  //   Transfer AC
  //   Transfer DR
  //   Over Flow of ASL
  //   The role of the encoder is to 
  //   convert the control signals to selection lines
  //   so, in the process, the arithmetic/ logical/ shift operations
  //   that are not present inside the BC ALU
  //   were replaced witha constant signal of 0
  //   since they can never be selected
endmodule

module BUS (
  input  INAR,
  input  CLRAR,
  input  CLRPC,
  input  INDR,
  input  CLRDR,
  input  AND,
  input  INAC,
  input  CIL,
  input  COM,
  input  CIR,
  input  LDTR,
  input  INTR,
  input  CLRTR,
  output [15:0] DR
);

  wire ADD, alu_1_e, CLAC, clk, d_ff_1_q, LDAC, LDAR, LDDR, LDIR, LDPC, PCINC, Read, TransDR, Write;
  wire [2:0] BUS;
  wire [11:0] AR_q, bit_extender_1_out, bit_extender_2_out, PC_q;
  wire [15:0] alu_1_ac_2, bit_extender_3_out, bit_extender_4_out, counter_2_q, IR, M, multiplexer_1_out, TR_q;

  main main_1 (
    .CLK(clk), .IR(IR), .DR(DR), .LDAC(LDAC), .CLAC(CLAC), .BUS(BUS), .WRITE(Write), .READ(Read),
    .LDPC(LDPC), .LDAR(LDAR), .LDDR(LDDR), .LDIR(LDIR), .TransferDR(TransDR), .ADD(ADD), .PCINC(PCINC));
  Clock clock_1 (.out(clk));
  ALU alu_1 (
    .AC(counter_2_q), .DR(DR), .AC_2(alu_1_ac_2), .E(alu_1_e), .AND(AND), .COM(COM), .CIR(CIR), .ADD(ADD),
    .Transfer_DR(TransDR), .CIL(CIL));  // open: V
  Bit_Extender #(.in_width(16), .out_width(12)) bit_extender_1 (.in(multiplexer_1_out), .out(bit_extender_1_out));
  Bit_Extender #(.in_width(16), .out_width(12)) bit_extender_2 (.in(multiplexer_1_out), .out(bit_extender_2_out));
  J_K_Flip_Flop j_k_ff_1 (.J(alu_1_e), .clk(clk), .preset(1'b0), .en(1'b1), .reset(1'b0));  // open: K, Q, Qn
  Counter #(.width(12), .max('hfff)) AR (
    .load(LDAR), .D(bit_extender_1_out), .count(INAR), .Q(AR_q), .clk(clk), .clr(CLRAR));  // open: carry
  Counter #(.width(12), .max('hfff)) PC (
    .load(LDPC), .D(bit_extender_2_out), .count(PCINC), .Q(PC_q), .clk(clk), .clr(CLRPC));  // open: carry
  Counter #(.width(16), .max('hffff)) counter_1 (
    .load(LDDR), .D(multiplexer_1_out), .count(INDR), .Q(DR), .clk(clk), .clr(CLRDR));  // open: carry
  Counter #(.width(16), .max('hffff)) counter_2 (
    .load(LDAC), .D(alu_1_ac_2), .count(INAC), .Q(counter_2_q), .clk(clk), .clr(d_ff_1_q));  // open: carry
  Counter #(.width(16), .max('hffff)) u_IR (
    .load(LDIR), .D(multiplexer_1_out), .count(1'b0), .Q(IR), .clk(clk), .clr(1'b0));  // open: carry
  Counter #(.width(16), .max('hffff)) TR (
    .load(LDTR), .D(multiplexer_1_out), .count(INTR), .Q(TR_q), .clk(clk), .clr(CLRTR));  // open: carry
  RAM #(.addrWidth(12), .dataWidth(16), .bus("separate")) ram_1 (
    .addr(AR_q), .din(multiplexer_1_out), .data(M), .str(Write), .sel(1'b1), .clk(clk), .ld(Read), .clr(1'b0));
  D_Flip_Flop d_ff_1 (.clk(clk), .D(CLAC), .Q(d_ff_1_q));  // open: Qn, preset, en, reset
  assign bit_extender_3_out = {{4{1'b0}}, AR_q};  // Bit_Extender bit_extender_3
  assign bit_extender_4_out = {{4{1'b0}}, PC_q};  // Bit_Extender bit_extender_4
  Multiplexer #(.select(3), .width(16), .enable("false")) multiplexer_1 (
    .in1(bit_extender_3_out), .in2(bit_extender_4_out), .in3(DR), .in4(counter_2_q), .in5(IR), .in6(TR_q),
    .in7(M), .out(multiplexer_1_out), .sel(BUS));  // open: in0

  // Notes on the sheet:
  //   MEM
  //   DR
  //   AC
endmodule
