// Logisim project XOR circuit.circ as structural Verilog: 1 circuit, main circuit main
module main (
  input  X,
  input  Y,
  output out_3
);

  wire X_prime_out, X_prime_Y_out, XY_prime_out, Y_prime_out;

  not X_prime (X_prime_out, X);
  not Y_prime (Y_prime_out, Y);
  and X_prime_Y (X_prime_Y_out, X_prime_out, Y);
  and XY_prime (XY_prime_out, X, Y_prime_out);
  or X_XOR_Y (out_3, X_prime_Y_out, XY_prime_out);
endmodule
