// Logisim project busSystemMux_17332.circ as structural Verilog: 1 circuit, main circuit main
module main (
  input  LDR1,
  input  INRR1,
  input  CLRR1,
  input  LDR2,
  input  INRR2,
  input  CLR2,
  input  [1:0] Selection_Lines,
  input  LDR3,
  input  INRR3,
  input  CLRR3,
  input  LDR4,
  input  INRR4,
  input  CLRR4
);

  wire clock_1_out;
  wire [15:0] counter_1_q, counter_2_q, counter_3_q, multiplexer_1_out, R3_q;

  Clock clock_1 (.out(clock_1_out));
  Counter #(.width(16), .max('hffff)) counter_1 (
    .load(LDR1), .D(multiplexer_1_out), .count(INRR1), .Q(counter_1_q), .clk(clock_1_out), .clr(CLRR1));  // open: carry
  Counter #(.width(16), .max('hffff)) counter_2 (
    .load(LDR2), .D(multiplexer_1_out), .count(INRR2), .Q(counter_2_q), .clk(clock_1_out), .clr(CLR2));  // open: carry
  Counter #(.width(16), .max('hffff)) R3 (
    .load(LDR3), .D(multiplexer_1_out), .count(INRR3), .Q(R3_q), .clk(clock_1_out), .clr(CLRR3));  // open: carry
  Counter #(.width(16), .max('hffff)) counter_3 (
    .load(LDR4), .D(multiplexer_1_out), .count(INRR4), .Q(counter_3_q), .clk(clock_1_out), .clr(CLRR4));  // open: carry
  Multiplexer #(.select(2), .width(16), .enable("false")) multiplexer_1 (
    .in0(counter_1_q), .in1(counter_2_q), .in2(R3_q), .in3(counter_3_q), .out(multiplexer_1_out),
    .sel(Selection_Lines));

  // Notes on the sheet:
  //   R1
  //   R2
  //   R3
  //   R4
endmodule
